# Fritzing sketch schema (saved by Fritzing 0.9.2b)
circuit board: 11.4159cm x 12.7204cm
breadboards: 1

parts:
  Componente1 = Arduino Mega 2560 (Rev3)
  Componente2 = Motor Driver 1A Dual TB6612FNG
  Motore_Sinistro = DC Motor
  J1 = Infrared Proximity Sensor
  Motore_Destro = DC Motor
  Contagiti_Motore_Destro = Contagiri motore rover 5
  Contagiti_Motore_Sinistro = Contagiri motore rover 5
  R1 = Photocell (LDR) [package=THT]
  VCC2 = Battery
  VCC5 = Battery
  VCC6 = Battery
  VCC7 = Battery
  VCC8 = Battery
  R2 = Resistor [tolerance=±5% resistance=10k package=THT]
  HC-SR04 = HC-SR04
  J2 = Basic Servo

nets:
  N1: Componente1.A0, J1.Vout
  GND: Componente1.GND, Componente2.GND, J1.GND, Contagiti_Motore_Destro.GND, Contagiti_Motore_Sinistro.GND, VCC5.-, R2.Pin_1
  N2: Componente1.D9_PWM, Componente2.PWMB
  VCC: Componente1.5V, Componente2.VCC, J1.Vcc, Contagiti_Motore_Destro.VIN, Contagiti_Motore_Sinistro.VIN, VCC6.+, HC-SR04.VCC, J2.vcc
  N3: Componente1.D3_PWM, Componente2.PWMA
  N4: Componente1.D26, J2.pulse
  N5: Componente1.D38, HC-SR04.ECHO
  N6: Componente1.D39, HC-SR04.TRIG
  N7: Componente1.D45, Componente2.STBY
  N8: Componente1.D46, Contagiti_Motore_Destro.Giallo
  N9: Componente1.D47, Contagiti_Motore_Destro.Bianco
  N10: Componente1.D48, Contagiti_Motore_Sinistro.Giallo
  N11: Componente1.D49, Contagiti_Motore_Sinistro.Bianco
  N12: Componente1.D50, Componente2.BIN1
  N13: Componente1.D51, Componente2.BIN2
  N14: Componente1.D52, Componente2.AIN2
  N15: Componente1.D53, Componente2.AIN1
  N16: Componente2.B01, Motore_Destro.pin_2
  N17: Componente2.B02, Motore_Destro.pin_1
  N18: Componente2.A02, Motore_Sinistro.pin_2
  N19: Componente2.A01, Motore_Sinistro.pin_1
  N20: R1.pin_1, R2.Pin_0
  N21: VCC2.+, VCC8.-
  N22: VCC7.-, VCC8.+

custom parts:
  Contagiri motore rover 5: Il contagiri dei nostri motori
